# Fritzing sketch circuito (saved by Fritzing 0.9.9b)
breadboards: 2

parts:
  Componente1 = Arduino Uno (Rev3) - ICSP
  Componente2 = Arduino Uno (Rev3) - ICSP
  S1 = Pushbutton [package="[THT]"]
  S2 = Pushbutton [package="[THT]"]
  S3 = Pushbutton [package="[THT]"]
  S4 = Pushbutton [package="[THT]"]
  R1 = Resistor [tolerance=±5% power=0.25 resistance=220 package=THT]
  LED1 = smd LED [color="Blue (430nm)" package="0603 [SMD]"]
  LED2 = smd LED [color="Red (633nm)" package="0603 [SMD]"]
  R2 = Resistor [tolerance=±5% power=0.25 resistance=220 package=THT]
  R3 = Resistor [tolerance=±5% power=0.25 resistance=220 package=THT]
  LED3 = smd LED [color="Green (555nm)" package="0603 [SMD]"]
  U1 = RF-LINK_TX [package=rf-link_tx]
  U2 = RF-LINK_RX [package=rf-link_rx]
  R4 = Resistor [tolerance=±5% power=0.25 resistance=220 package=THT]
  R5 = Resistor [tolerance=±5% power=0.25 resistance=220 package=THT]
  R6 = Resistor [tolerance=±5% power=0.25 resistance=220 package=THT]
  R7 = Resistor [tolerance=±5% power=0.25 resistance=220 package=THT]
  LED4 = smd LED [color="Green (555nm)" package="0603 [SMD]"]
  LED5 = smd LED [color="Red (633nm)" package="0603 [SMD]"]
  LED6 = smd LED [color="Blue (430nm)" package="0603 [SMD]"]
  R8 = Resistor [tolerance=±5% power=0.25 resistance=220 package=THT]
  R9 = Resistor [tolerance=±5% power=0.25 resistance=220 package=THT]
  R10 = Resistor [tolerance=±5% power=0.25 resistance=220 package=THT]

nets:
  N1: Componente1.D11_PWM/MOSI, U1.DATA
  N2: Componente1.D2, S4.Pin_1, S4.Pin_2, LED1.anode, R4.Pin_0
  N3: Componente1.D3_PWM, S3.Pin_1, S3.Pin_2, LED2.anode, R5.Pin_0
  N4: Componente1.D4, S2.Pin_1, S2.Pin_2, LED3.anode, R6.Pin_0
  N5: Componente1.D5_PWM, S1.Pin_1, S1.Pin_2, R7.Pin_0
  5V: Componente1.5V, S1.Pin_3, S1.Pin_4, S2.Pin_3, S2.Pin_4, S3.Pin_3, S3.Pin_4, S4.Pin_3, S4.Pin_4, U1.+5V
  GND: Componente1.GND, R1.Pin_1, R2.Pin_1, R3.Pin_1, U1.GND, R4.Pin_1, R5.Pin_1, R6.Pin_1, R7.Pin_1
  N6: Componente2.D2, LED6.anode
  N7: Componente2.D3_PWM, LED5.anode
  N8: Componente2.D4, LED4.anode
  5V_2: Componente2.5V, U2.+5V
  GND_2: Componente2.GND, U2.GND
  N9: R1.Pin_0, LED1.cathode
  N10: LED2.cathode, R2.Pin_0
  N11: R3.Pin_0, LED3.cathode
  N12: LED4.cathode, R10.Pin_0
  N13: LED5.cathode, R9.Pin_0
  N14: LED6.cathode, R8.Pin_0
  N15: R8.Pin_1, R9.Pin_1, R10.Pin_1

notes:
  botaoAzul 2
  botaoVermelho 3
  botaoVerde 4
  botaoEnviar 5
  Azul 2
  Vermelho 3
  Verde 4
